# Fritzing sketch 完整線路圖new (saved by Fritzing 0.9.2b)
breadboards: 2

parts:
  Q1 = NPN-Transistor [package="TO92 [THT]"]
  SPKR1 = Loudspeaker
  R1 = Resistor [tolerance=±5% resistance=330 package=THT]
  元件1 = Arduino Uno (Rev3)
  LED3 = LED - 5mm [color="Yellow (592nm)" package="5 mm [THT]"]
  Q2 = NPN-Transistor [package="TO92 [THT]"]
  LED4 = LED - 5mm [color="Yellow (592nm)" package="5 mm [THT]"]
  SPKR2 = Loudspeaker
  R2 = Resistor [tolerance=±5% resistance=330 package=THT]
  LED5 = LED - 5mm [color="Red (635nm)" package="5 mm [THT]"]
  LED6 = LED - 5mm [color="Red (635nm)" package="5 mm [THT]"]
  U1 = Barometric Pressure Sensor
  U2 = Barometric Pressure Sensor

nets:
  N1: Q1.E, Q2.E, U1.DRDY, U2.DRDY
  N2: Q1.B, 元件1.D7
  N3: Q1.C, SPKR2.pin2
  GND: SPKR1.pin1, LED3.cathode, LED4.cathode, SPKR2.pin1, LED5.cathode, LED6.cathode, U1.GND, U2.GND
  N4: SPKR1.pin2, Q2.C
  N5: R1.Pin_0, LED3.anode, LED6.anode
  N6: R1.Pin_1, 元件1.D6_PWM
  N7: 元件1.D8, U2.MISO
  N8: 元件1.D10_PWM/SS, R2.Pin_0
  N9: 元件1.D11_PWM/MOSI, Q2.B
  N10: LED4.anode, LED5.anode
